// Logisim project Address Decode.circ as structural Verilog: 8 circuits, main circuit Scratchpad
module Scratchpad (
  input  VPB,
  input  in_2,
  input  in_3,
  input  in_4,
  input  in_5,
  input  in_6,
  input  in_7,
  input  in_8,
  input  in_9,
  input  in_10,
  input  in_11,
  input  in_12,
  input  in_13,
  input  in_14,
  input  in_15,
  input  in_16,
  input  in_17,
  input  in_18,
  input  in_19,
  input  in_20,
  input  in_21,
  input  in_22,
  input  in_23,
  input  in_24,
  input  in_25
);

  wire and_1_out, and_2_out, and_3_out, and_4_out, comparator_1_gt, comparator_2_eq, counter_1_carry,
       d_ff_1_q, INT, IRQ, NMI, not_2_out, not_3_out, not_4_out, not_5_out, or_1_out, or_2_out, or_3_out,
       PHI2, pull_resistor_1_node, pull_resistor_2_node, pull_resistor_3_node, pull_resistor_5_node,
       pull_resistor_8_node, pull_resistor_9_node, pull_resistor_11_node, pull_resistor_15_node,
       pull_resistor_16_node, R_WB_out, undriven, undriven_2, undriven_3, undriven_4, undriven_5, undriven_6,
       VPB_t;
  wire [2:0] priority_encoder_1_out, priority_encoder_3_out;
  wire [3:0] controlled_buffer_2_out, controlled_buffer_4_out, counter_2_q, pull_resistor_7_node;
  wire [3:3] pull_resistor_4_node, pull_resistor_6_node;
  wire [7:0] Address_out, controlled_buffer_1_out, pull_resistor_10_node, register_1_q;
  wire [15:0] Address_2_out, multiplexer_1_out;
  wire [15:15] pull_resistor_12_node;

  Pull_Resistor #(.pull(1)) pull_resistor_1 (.node(pull_resistor_1_node));
  Counter #(.width(2), .max('h3)) counter_1 (.carry(counter_1_carry), .clk(PHI2));  // open: load, D, count, Q, clr
  Clock clock_1 (.out(PHI2));
  LED u_NMI (.in(NMI));
  LED u_IRQ (.in(IRQ));
  Pull_Resistor #(.pull(1)) pull_resistor_2 (.node(pull_resistor_2_node));
  Pull_Resistor #(.pull(1)) pull_resistor_3 (.node(pull_resistor_3_node));
  Random Address (.clk(counter_1_carry), .next(pull_resistor_1_node), .out(Address_out));  // open: clr
  Counter #(.width(4), .max('hf)) counter_2 (
    .D(4'b0000), .Q(counter_2_q), .clk(PHI2), .clr(or_1_out));  // open: load, count, carry
  or or_1 (or_1_out, INT, comparator_2_eq);
  or or_2 (or_2_out, VPB, comparator_1_gt);
  not not_1 (VPB_t, or_2_out);
  Register #(.trigger("high")) Bank_Address (.D({8{1'b0}}), .clk(counter_1_carry));  // open: en, Q, clr
  Random #(.width(16)) Address_2 (
    .clk(counter_1_carry), .next(pull_resistor_2_node), .out(Address_2_out));  // open: clr
  not not_2 (not_2_out, R_WB_out);
  Random #(.width(1)) R_WB (.clk(counter_1_carry), .next(pull_resistor_3_node), .out(R_WB_out));  // open: clr
  // Probe on controlled_buffer_1_out
  // Probe on Address_out
  Comparator #(.width(4), .mode("unsigned")) comparator_1 (
    .a(counter_2_q), .b(4'b0101), .gt(comparator_1_gt));  // open: eq, lt
  Comparator #(.width(4), .mode("unsigned")) comparator_2 (
    .a(counter_2_q), .b(4'b1000), .eq(comparator_2_eq));  // open: gt, lt
  or or_3 (or_3_out, not_2_out, INT);
  not not_3 (not_3_out, or_3_out);
  assign controlled_buffer_1_out = not_3_out ? Address_out : 8'bz;  // Controlled_Buffer controlled_buffer_1
  Pull_Resistor pull_resistor_4 (.node(pull_resistor_4_node[3]));
  // Probe on priority_encoder_1_out
  Priority_Encoder #(.disabled(0)) priority_encoder_1 (
    .in0(in_2), .in1(in_3), .in2(in_4), .in3(in_5), .in4(in_6), .in5(in_7), .in6(in_8), .in7(in_9),
    .out(priority_encoder_1_out), .en_in(pull_resistor_5_node));
  assign controlled_buffer_2_out = and_1_out ? {pull_resistor_4_node[3], priority_encoder_1_out} : 4'bz;  // Controlled_Buffer controlled_buffer_2
  and and_1 (and_1_out, undriven, not_4_out);
  not not_4 (not_4_out, undriven_2);
  Pull_Resistor #(.pull(1)) pull_resistor_5 (.node(pull_resistor_5_node));
  not Interrupt (INT, and_2_out);
  and and_2 (and_2_out, undriven_3, undriven_6, undriven_4);
  Pull_Resistor pull_resistor_6 (.node(pull_resistor_6_node[3]));
  assign controlled_buffer_2_out = and_3_out ? pull_resistor_7_node : 4'bz;  // Controlled_Buffer controlled_buffer_3
  Pull_Resistor #(.pull(1)) pull_resistor_7 (.node(pull_resistor_7_node[3]));
  Priority_Encoder #(.disabled(0)) priority_encoder_2 (
    .in0(in_10), .in1(in_11), .in2(in_12), .in3(in_13), .in4(in_14), .in5(in_15), .in6(in_16), .in7(in_17),
    .out(pull_resistor_7_node[2:0]), .en_in(pull_resistor_8_node));
  assign controlled_buffer_4_out = and_3_out ? {4{pull_resistor_6_node[3]}} : 4'bz;  // Controlled_Buffer controlled_buffer_4
  // Probe on pull_resistor_7_node[2:0]
  or or_4 (IRQ, undriven, undriven_5);
  Pull_Resistor #(.pull(1)) pull_resistor_8 (.node(pull_resistor_8_node));
  // Probe on {controlled_buffer_4_out[3:1], controlled_buffer_2_out, controlled_buffer_4_out[0]}
  D_Flip_Flop #(.trigger("high")) d_ff_1 (
    .clk(PHI2), .D(IRQ), .Q(d_ff_1_q), .en(pull_resistor_9_node));  // open: Qn, preset, reset
  Pull_Resistor #(.pull(1)) pull_resistor_9 (.node(pull_resistor_9_node));
  and and_3 (and_3_out, undriven_5, not_5_out);
  Register #(.trigger("high")) register_1 (
    .D({controlled_buffer_4_out[3:1], controlled_buffer_2_out, controlled_buffer_4_out[0]}),
    .Q(register_1_q), .clk(and_4_out));  // open: en, clr
  and and_4 (and_4_out, VPB_t, d_ff_1_q);
  assign {controlled_buffer_4_out[3:1], controlled_buffer_2_out, controlled_buffer_4_out[0]} = NMI ? {{2{pull_resistor_10_node[7]}}, pull_resistor_10_node[5], pull_resistor_10_node[7], priority_encoder_3_out, pull_resistor_10_node[0]} : 8'bz;  // Controlled_Buffer controlled_buffer_5
  not not_5 (not_5_out, NMI);
  // Probe on {{2{pull_resistor_10_node[7]}}, pull_resistor_10_node[5], pull_resistor_10_node[7], priority_encoder_3_out, pull_resistor_10_node[0]}
  Pull_Resistor pull_resistor_10 (.node(pull_resistor_10_node[0]));
  // Probe on priority_encoder_3_out
  Priority_Encoder #(.disabled(0)) priority_encoder_3 (
    .in0(in_18), .in1(in_19), .in2(in_20), .in3(in_21), .in4(in_22), .in5(in_23), .in6(in_24), .in7(in_25),
    .out(priority_encoder_3_out), .en_in(pull_resistor_11_node));
  Pull_Resistor #(.pull(1)) pull_resistor_11 (.node(pull_resistor_11_node));
  Pull_Resistor #(.pull(1)) pull_resistor_12 (.node(pull_resistor_12_node[15]));
  Pull_Resistor #(.pull(1)) pull_resistor_13 (.node(pull_resistor_10_node[5]));
  Pull_Resistor pull_resistor_14 (.node(pull_resistor_10_node[7]));
  // Probe on Address_2_out
  Pull_Resistor #(.pull(1)) pull_resistor_15 (.node(pull_resistor_15_node));
  // Probe on {{8{pull_resistor_12_node[15]}}, register_1_q}
  // Probe on multiplexer_1_out
  Multiplexer #(.width(16)) multiplexer_1 (
    .in0(Address_2_out), .in1({{8{pull_resistor_12_node[15]}}, register_1_q}), .out(multiplexer_1_out),
    .sel(INT), .en(pull_resistor_15_node));
  Pull_Resistor #(.pull(1)) pull_resistor_16 (.node(pull_resistor_16_node));
  RAM #(.addrWidth(16)) ram_1 (
    .addr(multiplexer_1_out), .data(controlled_buffer_1_out), .sel(pull_resistor_16_node), .clk(PHI2),
    .ld(or_3_out));  // open: clr
endmodule

module CPU_Board (
  input  in_1,
  input  in_2,
  input  in_3,
  input  in_4,
  input  in_5,
  input  in_6,
  input  in_7,
  input  in_8,
  input  in_9,
  input  in_10,
  input  in_11,
  input  in_12,
  input  in_13,
  input  in_14,
  input  in_15,
  input  in_16
);

  wire interrupt_decode_1_int, interrupt_select_1_irqb, interrupt_select_1_nmib, not_1_out, PHI2,
       pull_resistor_1_node, pull_resistor_3_node, w65c816s_1_da, w65c816s_1_pa, w65c816s_1_r_wb,
       w65c816s_1_vpb;
  wire [3:0] interrupt_decode_1_int_addr0;
  wire [7:0] controlled_buffer_1_out, controlled_buffer_2_out, pull_resistor_2_node, w65c816s_1_addr0,
       w65c816s_1_addr8, w65c816s_1_addr16, w65c816s_1_data7__w;

  Clock u_PHI2 (.out(PHI2));
  Pull_Resistor pull_resistor_1 (.node(pull_resistor_1_node));
  Pull_Resistor pull_resistor_2 (.node(pull_resistor_2_node));
  Pull_Resistor pull_resistor_3 (.node(pull_resistor_3_node));
  Interrupt_Select interrupt_select_1 (
    .INT_ADDR0(interrupt_decode_1_int_addr0[0]), .INT_ADDR1(interrupt_decode_1_int_addr0[1]),
    .INT_ADDR2(interrupt_decode_1_int_addr0[2]), .INT_ADDR3(interrupt_decode_1_int_addr0[3]),
    .INT(interrupt_decode_1_int), .Write(pull_resistor_1_node), .D0(pull_resistor_2_node[0]),
    .D1(pull_resistor_2_node[1]), .D2(pull_resistor_2_node[2]), .D3(pull_resistor_2_node[3]),
    .D4(pull_resistor_2_node[4]), .D5(pull_resistor_2_node[5]), .D6(pull_resistor_2_node[6]),
    .D7(pull_resistor_2_node[7]), .NMIB(interrupt_select_1_nmib), .IRQB(interrupt_select_1_irqb), .PHI2(PHI2));
  Interrupt_Decode interrupt_decode_1 (
    .INT0(in_1), .INT1(in_2), .INT2(in_3), .INT3(in_4), .INT4(in_5), .INT5(in_6), .INT6(in_7), .INT7(in_8),
    .INT8(in_9), .INT9(in_10), .INT10(in_11), .INT11(in_12), .INT12(in_13), .INT13(in_14), .INT14(in_15),
    .INT15(in_16), .VPB(pull_resistor_3_node), .INT_ADDR0(interrupt_decode_1_int_addr0[0]),
    .INT_ADDR1(interrupt_decode_1_int_addr0[1]), .INT_ADDR2(interrupt_decode_1_int_addr0[2]),
    .INT_ADDR3(interrupt_decode_1_int_addr0[3]), .INT(interrupt_decode_1_int));
  // Probe on {w65c816s_1_addr16, w65c816s_1_addr8, w65c816s_1_addr0}
  W65C816S w65c816s_1 (
    .PHI2(PHI2), .NMIB(interrupt_select_1_nmib), .IRQB(interrupt_select_1_irqb),
    .DATA0__R(controlled_buffer_1_out[7]), .DATA1__R(controlled_buffer_1_out[6]),
    .DATA2__R(controlled_buffer_1_out[5]), .DATA3__R(controlled_buffer_1_out[4]),
    .DATA4__R(controlled_buffer_1_out[3]), .DATA5__R(controlled_buffer_1_out[2]),
    .DATA6__R(controlled_buffer_1_out[1]), .DATA7__R(controlled_buffer_1_out[0]),
    .DATA0__W(w65c816s_1_data7__w[7]), .DATA1__W(w65c816s_1_data7__w[6]), .DATA2__W(w65c816s_1_data7__w[5]),
    .DATA3__W(w65c816s_1_data7__w[4]), .DATA4__W(w65c816s_1_data7__w[3]), .DATA5__W(w65c816s_1_data7__w[2]),
    .DATA6__W(w65c816s_1_data7__w[1]), .DATA7__W(w65c816s_1_data7__w[0]), .R_WB(w65c816s_1_r_wb),
    .ADDR0(w65c816s_1_addr0[0]), .ADDR1(w65c816s_1_addr0[1]), .ADDR2(w65c816s_1_addr0[2]),
    .ADDR3(w65c816s_1_addr0[3]), .ADDR4(w65c816s_1_addr0[4]), .ADDR5(w65c816s_1_addr0[5]),
    .ADDR6(w65c816s_1_addr0[6]), .ADDR7(w65c816s_1_addr0[7]), .ADDR8(w65c816s_1_addr8[0]),
    .ADDR9(w65c816s_1_addr8[1]), .ADDR10(w65c816s_1_addr8[2]), .ADDR11(w65c816s_1_addr8[3]),
    .ADDR12(w65c816s_1_addr8[4]), .ADDR13(w65c816s_1_addr8[5]), .ADDR14(w65c816s_1_addr8[6]),
    .ADDR15(w65c816s_1_addr8[7]), .ADDR16(w65c816s_1_addr16[0]), .ADDR17(w65c816s_1_addr16[1]),
    .ADDR18(w65c816s_1_addr16[2]), .ADDR19(w65c816s_1_addr16[3]), .ADDR20(w65c816s_1_addr16[4]),
    .ADDR21(w65c816s_1_addr16[5]), .ADDR22(w65c816s_1_addr16[6]), .ADDR23(w65c816s_1_addr16[7]),
    .DA(w65c816s_1_da), .PA(w65c816s_1_pa), .VPB(w65c816s_1_vpb));
  assign controlled_buffer_1_out = w65c816s_1_r_wb ? controlled_buffer_2_out : 8'bz;  // Controlled_Buffer controlled_buffer_1
  not not_1 (not_1_out, w65c816s_1_r_wb);
  assign controlled_buffer_2_out = not_1_out ? w65c816s_1_data7__w : 8'bz;  // Controlled_Buffer controlled_buffer_2
  // Probe on controlled_buffer_2_out

  // Notes on the sheet:
  //   Address         Bus
  //   N MIB
  //   IRQ B
  //   W65C816
  //   D A
  //   P A
  //   VP B
  //   R WB
  //   Data  Bus
endmodule

module W65C816S (
  input  DATA0__R,
  input  DATA1__R,
  input  DATA2__R,
  input  DATA3__R,
  input  DATA4__R,
  input  DATA5__R,
  input  DATA6__R,
  input  DATA7__R,
  input  PHI2,
  input  NMIB,
  input  IRQB,
  output DATA0__W,
  output DATA1__W,
  output DATA2__W,
  output DATA3__W,
  output DATA4__W,
  output DATA5__W,
  output DATA6__W,
  output DATA7__W,
  output R_WB,
  output ADDR0,
  output ADDR1,
  output ADDR2,
  output ADDR3,
  output ADDR4,
  output ADDR5,
  output ADDR6,
  output ADDR7,
  output ADDR8,
  output ADDR9,
  output ADDR10,
  output ADDR11,
  output ADDR12,
  output ADDR13,
  output ADDR14,
  output ADDR15,
  output ADDR16,
  output ADDR17,
  output ADDR18,
  output ADDR19,
  output ADDR20,
  output ADDR21,
  output ADDR22,
  output ADDR23,
  output DA,
  output PA,
  output VPB
);

  wire and_1_out, and_2_out, and_3_out, and_4_out, clock_1_out, counter_1_carry, Interrupt_Emulation_r_wb,
       not_1_out, not_2_out, not_3_out, or_1_out, or_2_out, Program_Emulation_busy, register_1_q;
  wire [2:0] counter_1_q;
  wire [7:0] controlled_buffer_1_out;

  Clock clock_1 (.out(clock_1_out));
  Counter #(.width(3), .max('h7)) counter_1 (
    .Q(counter_1_q), .carry(counter_1_carry), .clk(clock_1_out));  // open: load, D, count, clr
  not not_1 (not_1_out, and_1_out);
  and and_1 (and_1_out, NMIB, IRQB);
  Register #(.width(1), .trigger("high")) register_1 (
    .D(not_1_out), .Q(register_1_q), .clk(not_1_out), .clr(and_2_out));  // open: en
  and and_2 (and_2_out, and_1_out, not_3_out);
  or or_1 (or_1_out, Program_Emulation_busy, Interrupt_Emulation_r_wb);
  not not_2 (not_2_out, or_1_out);
  and and_3 (and_3_out, clock_1_out, register_1_q);
  and and_4 (and_4_out, clock_1_out, or_2_out);
  or or_2 (or_2_out, not_2_out, Program_Emulation_busy);
  not not_3 (not_3_out, Interrupt_Emulation_r_wb);
  MPU_PRG_Emulation Program_Emulation (
    .PHI2(and_4_out),
    .DATA({DATA7__W, DATA6__W, DATA5__W, DATA4__W, DATA3__W, DATA2__W, DATA1__W, DATA0__W}), .R_WB(R_WB),
    .ADDR({ADDR15, ADDR14, ADDR13, ADDR12, ADDR11, ADDR10, ADDR9, ADDR8, ADDR7, ADDR6, ADDR5, ADDR4, ADDR3, ADDR2, ADDR1, ADDR0}),
    .DA(DA), .PA(PA), .BUSY(Program_Emulation_busy));
  MPU_INT_Emulation Interrupt_Emulation (
    .PHI2(and_3_out), .IRQB(NMIB), .NMIB(IRQB), .R_WB(Interrupt_Emulation_r_wb));  // open: DATA, BUSY, ADDR, DA, PA
  assign controlled_buffer_1_out = R_WB ? {DATA7__R, DATA6__R, DATA5__R, DATA4__R, DATA3__R, DATA2__R, DATA1__R, DATA0__R} : 8'bz;  // Controlled_Buffer controlled_buffer_1
  Pull_Resistor pull_resistor_1 (.node(ADDR16));

  assign ADDR17 = ADDR16;
  assign ADDR18 = ADDR16;
  assign ADDR19 = ADDR16;
  assign ADDR20 = ADDR16;
  assign ADDR21 = ADDR16;
  assign ADDR22 = ADDR16;
  assign ADDR23 = ADDR16;
endmodule

module Interrupt_Decode (
  input  VPB,
  input  INT0,
  input  INT1,
  input  INT2,
  input  INT3,
  input  INT4,
  input  INT5,
  input  INT6,
  input  INT7,
  input  INT8,
  input  INT9,
  input  INT10,
  input  INT11,
  input  INT12,
  input  INT13,
  input  INT14,
  input  INT15,
  output INT_ADDR0,
  output INT_ADDR1,
  output INT_ADDR2,
  output INT_ADDR3,
  output INT
);

  wire and_1_out, and_2_out, not_1_out, not_2_out, pull_resistor_2_node, pull_resistor_4_node, undriven,
       undriven_2;
  wire [3:0] controlled_buffer_1_out, pull_resistor_1_node, pull_resistor_3_node, register_1_q;

  Pull_Resistor pull_resistor_1 (.node(pull_resistor_1_node[3]));
  assign controlled_buffer_1_out = and_1_out ? pull_resistor_1_node : 4'bz;  // Controlled_Buffer controlled_buffer_1
  and and_1 (and_1_out, undriven, not_1_out);
  not not_1 (not_1_out, undriven_2);
  // Probe on pull_resistor_1_node[2:0]
  Priority_Encoder #(.disabled(0)) priority_encoder_1 (
    .in0(INT0), .in1(INT1), .in2(INT2), .in3(INT3), .in4(INT4), .in5(INT5), .in6(INT6), .in7(INT7),
    .out(pull_resistor_1_node[2:0]), .en_in(pull_resistor_2_node));
  Pull_Resistor #(.pull(1)) pull_resistor_2 (.node(pull_resistor_2_node));
  Pull_Resistor #(.pull(1)) pull_resistor_3 (.node(pull_resistor_3_node[3]));
  // Probe on pull_resistor_3_node[2:0]
  Priority_Encoder #(.disabled(0)) priority_encoder_2 (
    .in0(INT8), .in1(INT9), .in2(INT10), .in3(INT11), .in4(INT12), .in5(INT13), .in6(INT14), .in7(INT15),
    .out(pull_resistor_3_node[2:0]), .en_in(pull_resistor_4_node));
  // Probe on controlled_buffer_1_out
  // Probe on controlled_buffer_1_out
  assign controlled_buffer_1_out = undriven_2 ? pull_resistor_3_node : 4'bz;  // Controlled_Buffer controlled_buffer_2
  Pull_Resistor #(.pull(1)) pull_resistor_4 (.node(pull_resistor_4_node));
  // Probe on controlled_buffer_1_out
  and and_2 (and_2_out, not_2_out, INT);
  not not_2 (not_2_out, VPB);
  or or_1 (INT, undriven, undriven_2);
  assign {INT_ADDR3, INT_ADDR2, INT_ADDR1, INT_ADDR0} = INT ? register_1_q : 4'bz;  // Controlled_Buffer controlled_buffer_3
  Register #(.width(4), .trigger("high")) register_1 (
    .D(controlled_buffer_1_out), .Q(register_1_q), .clk(and_2_out));  // open: en, clr
endmodule

module Interrupt_Select (
  input  PHI2,
  input  INT_ADDR0,
  input  INT_ADDR1,
  input  INT_ADDR2,
  input  INT_ADDR3,
  input  INT,
  input  Write,
  input  D0,
  input  D1,
  input  D2,
  input  D3,
  input  D4,
  input  D5,
  input  D6,
  input  D7,
  output NMIB,
  output IRQB
);

  wire IRQ0_q, IRQ1_q, IRQ2_q, IRQ3_q, IRQ4_q, IRQ5_q, IRQ6_q, IRQ7_q, multiplexer_1_out, not_1_out,
       not_2_out, not_3_out, or_1_out, pull_resistor_1_node;

  not not_1 (not_1_out, INT);
  not not_2 (not_2_out, Write);
  D_Flip_Flop #(.trigger("high")) IRQ0 (.clk(not_2_out), .D(D0), .Q(IRQ0_q));  // open: Qn, preset, en, reset
  D_Flip_Flop #(.trigger("high")) IRQ1 (.clk(not_2_out), .D(D1), .Q(IRQ1_q));  // open: Qn, preset, en, reset
  D_Flip_Flop #(.trigger("high")) IRQ2 (.clk(not_2_out), .D(D2), .Q(IRQ2_q));  // open: Qn, preset, en, reset
  D_Flip_Flop #(.trigger("high")) IRQ3 (.clk(not_2_out), .D(D3), .Q(IRQ3_q));  // open: Qn, preset, en, reset
  D_Flip_Flop #(.trigger("high")) IRQ4 (.clk(not_2_out), .D(D4), .Q(IRQ4_q));  // open: Qn, preset, en, reset
  D_Flip_Flop #(.trigger("high")) IRQ5 (.clk(not_2_out), .D(D5), .Q(IRQ5_q));  // open: Qn, preset, en, reset
  D_Flip_Flop #(.trigger("high")) IRQ6 (.clk(not_2_out), .D(D6), .Q(IRQ6_q));  // open: Qn, preset, en, reset
  D_Flip_Flop #(.trigger("high")) IRQ7 (.clk(not_2_out), .D(D7), .Q(IRQ7_q));  // open: Qn, preset, en, reset
  // Probe on {INT_ADDR2, INT_ADDR1, INT_ADDR0}
  Pull_Resistor #(.pull(1)) pull_resistor_1 (.node(pull_resistor_1_node));
  or or_1 (or_1_out, INT_ADDR3, multiplexer_1_out);
  Multiplexer #(.select(3)) multiplexer_1 (
    .in0(IRQ0_q), .in1(IRQ1_q), .in2(IRQ2_q), .in3(IRQ3_q), .in4(IRQ4_q), .in5(IRQ5_q), .in6(IRQ6_q),
    .in7(IRQ7_q), .out(multiplexer_1_out), .sel({INT_ADDR2, INT_ADDR1, INT_ADDR0}), .en(pull_resistor_1_node));
  not not_3 (not_3_out, or_1_out);
  or or_2 (NMIB, not_1_out, or_1_out);
  or or_3 (IRQB, not_3_out, not_1_out);
endmodule

module MPU_INT_Emulation (
  input  PHI2,
  input  IRQB,
  input  NMIB,
  output [7:0] DATA,
  output BUSY,
  output R_WB,
  output [15:0] ADDR,
  output DA,
  output PA
);

  wire comparator_1_eq, counter_1_carry, not_1_out, not_2_out, not_3_out, not_4_out, range_test_2_out_4;
  wire [2:0] counter_1_q;
  wire [7:0] counter_2_q, Write_Data_out;
  wire [15:0] adder_1_out, controlled_buffer_1_out, controlled_buffer_3_out;

  not not_1 (not_1_out, NMIB);
  assign controlled_buffer_1_out = not_1_out ? 16'hffea : 16'bz;  // Controlled_Buffer controlled_buffer_1
  not not_2 (not_2_out, IRQB);
  assign controlled_buffer_1_out = not_2_out ? 16'hffee : 16'bz;  // Controlled_Buffer controlled_buffer_2
  Counter #(.width(3), .max('h6)) counter_1 (
    .Q(counter_1_q), .carry(counter_1_carry), .clk(PHI2));  // open: load, D, count, clr
  Comparator #(.width(3), .mode("unsigned")) comparator_1 (
    .a(counter_1_q), .b(3'b101), .eq(comparator_1_eq));  // open: gt, lt
  Range_Test range_test_1 (.MIN(3'b010), .MAX(3'b100), .out_4(DA), .D(counter_1_q));
  Counter counter_2 (.Q(counter_2_q), .clk(PHI2), .clr(counter_1_carry));  // open: load, D, count, carry
  Range_Test range_test_2 (.MIN(3'b000), .MAX(3'b001), .out_4(range_test_2_out_4), .D(counter_1_q));
  Range_Test range_test_3 (.MIN(3'b101), .MAX(3'b110), .out_4(PA), .D(counter_1_q));
  assign controlled_buffer_3_out = comparator_1_eq ? {16{1'b0}} : 16'bz;  // Controlled_Buffer controlled_buffer_3
  not not_3 (not_3_out, comparator_1_eq);
  assign controlled_buffer_3_out = not_3_out ? 16'h1 : 16'bz;  // Controlled_Buffer controlled_buffer_4
  assign DATA = not_4_out ? Write_Data_out : 8'bz;  // Controlled_Buffer controlled_buffer_5
  Random Write_Data (.clk(not_4_out), .out(Write_Data_out));  // open: next, clr
  not not_4 (not_4_out, R_WB);
  Counter #(.width(1), .max('h1)) counter_3 (.Q(R_WB), .clk(counter_1_carry));  // open: load, D, count, carry, clr
  assign ADDR = DA ? {8'h1, counter_2_q} : 16'bz;  // Controlled_Buffer controlled_buffer_6
  assign ADDR = range_test_2_out_4 ? 16'hcece : 16'bz;  // Controlled_Buffer controlled_buffer_7
  assign ADDR = PA ? adder_1_out : 16'bz;  // Controlled_Buffer controlled_buffer_8
  Adder #(.width(16)) adder_1 (
    .a(controlled_buffer_1_out), .b(controlled_buffer_3_out), .out(adder_1_out));  // open: cin, cout
  not not_5 (BUSY, counter_1_carry);
  // Probe on ADDR

  // Notes on the sheet:
  //   DA
  //   None
  //   DA
endmodule

module MPU_PRG_Emulation (
  input  PHI2,
  output [7:0] DATA,
  output BUSY,
  output R_WB,
  output [15:0] ADDR,
  output DA,
  output PA
);

  wire comparator_1_eq, comparator_2_eq, counter_1_carry, not_1_out, not_2_out, or_1_out,
       pull_resistor_1_node, range_test_2_out_4, undriven;
  wire [2:0] counter_1_q;
  wire [7:0] Write_Data_out;
  wire [15:0] adder_1_out, Address_out, controlled_buffer_1_out, counter_3_q;

  Counter #(.width(3), .max('h7)) counter_1 (
    .Q(counter_1_q), .carry(counter_1_carry), .clk(PHI2));  // open: load, D, count, clr
  Random #(.width(16)) Address (.clk(counter_1_carry), .next(pull_resistor_1_node), .out(Address_out));  // open: clr
  Pull_Resistor #(.pull(1)) pull_resistor_1 (.node(pull_resistor_1_node));
  Comparator #(.width(3), .mode("unsigned")) comparator_1 (
    .a(counter_1_q), .b(3'b111), .eq(comparator_1_eq));  // open: gt, lt
  Range_Test range_test_1 (.MIN(3'b000), .MAX(3'b001), .out_4(PA), .D(counter_1_q));
  or or_1 (or_1_out, counter_1_carry, comparator_2_eq);
  Comparator #(.width(3), .mode("unsigned")) comparator_2 (
    .a(counter_1_q), .b(3'b001), .eq(comparator_2_eq));  // open: gt, lt
  Range_Test range_test_2 (.MIN(3'b010), .MAX(3'b011), .out_4(range_test_2_out_4), .D(counter_1_q));
  Range_Test range_test_3 (.MIN(3'b100), .MAX(3'b111), .out_4(DA), .D(counter_1_q));
  assign controlled_buffer_1_out = comparator_1_eq ? {16{1'b0}} : 16'bz;  // Controlled_Buffer controlled_buffer_1
  not not_1 (not_1_out, comparator_1_eq);
  assign controlled_buffer_1_out = not_1_out ? 16'h1 : 16'bz;  // Controlled_Buffer controlled_buffer_2
  assign DATA = not_2_out ? Write_Data_out : 8'bz;  // Controlled_Buffer controlled_buffer_3
  Random Write_Data (.clk(not_2_out), .next(undriven), .out(Write_Data_out));  // open: clr
  not not_2 (not_2_out, R_WB);
  Counter #(.width(1), .max('h1)) counter_2 (.Q(R_WB), .clk(counter_1_carry));  // open: load, D, count, carry, clr
  assign ADDR = PA ? counter_3_q : 16'bz;  // Controlled_Buffer controlled_buffer_4
  Counter #(.width(16), .max('hffff)) counter_3 (.Q(counter_3_q), .clk(or_1_out));  // open: load, D, count, carry, clr
  assign ADDR = range_test_2_out_4 ? 16'hcece : 16'bz;  // Controlled_Buffer controlled_buffer_5
  assign ADDR = DA ? adder_1_out : 16'bz;  // Controlled_Buffer controlled_buffer_6
  Adder #(.width(16)) adder_1 (.a(Address_out), .b(controlled_buffer_1_out), .out(adder_1_out));  // open: cin, cout
  not not_3 (BUSY, counter_1_carry);
  // Probe on ADDR

  // Notes on the sheet:
  //   PA
  //   None
  //   DA
endmodule

module Range_Test (
  input  [2:0] MIN,
  input  [2:0] D,
  input  [2:0] MAX,
  output out_4
);

  wire comparator_1_eq, comparator_1_gt, comparator_2_eq, comparator_2_lt, or_1_out, or_2_out;

  Comparator #(.width(3), .mode("unsigned")) comparator_1 (
    .a(D), .b(MIN), .gt(comparator_1_gt), .eq(comparator_1_eq));  // open: lt
  Comparator #(.width(3), .mode("unsigned")) comparator_2 (
    .a(D), .b(MAX), .eq(comparator_2_eq), .lt(comparator_2_lt));  // open: gt
  or or_1 (or_1_out, comparator_1_gt, comparator_1_eq);
  or or_2 (or_2_out, comparator_2_eq, comparator_2_lt);
  and and_1 (out_4, or_1_out, or_2_out);
endmodule
