// Logisim project DeviceDecode.circ as structural Verilog: 1 circuit, main circuit main
module main (
  input  [16:0] in_1
);

  wire Device_RAM, Device_Registers, Device_ROM, nor_1_out, not_1_out, not_2_out;

  // Probe on in_1
  not not_1 (not_1_out, in_1[16]);
  not not_2 (not_2_out, in_1[15]);
  nor nor_1 (nor_1_out, in_1[14], in_1[13], in_1[12], in_1[11], in_1[10]);
  Comparator #(.mode("unsigned")) comparator_1 (.a(8'h1), .b(in_1[16:9]), .eq(Device_Registers));  // open: gt, lt
  Comparator #(.mode("unsigned")) comparator_2 (.a({8{1'b0}}), .b(in_1[16:9]), .eq(Device_ROM));  // open: gt, lt
  nand nand_1 (Device_RAM, not_1_out, not_2_out, nor_1_out);
endmodule
