// Logisim project Memory_Copier.circ as structural Verilog: 1 circuit, main circuit main
module main (
);

  wire CLK, clock_1_out, clock_2_out, CNT, d_ff_1_q, d_ff_1_qn, d_ff_2_q, ds1813_1_p2, f521_1_p4, FOUR_BIT,
       LE, lvc161_1_p8, lvc161_2_p8, lvc161_3_p8, lvc161_4_p8, lvc161_5_p8, lvc161_6_p8, lvc573_1_p4,
       lvc4245_1_p4, not_1_out, not_6_out, or_1_out, or_2_out, PEB, pull_resistor_4_node,
       pull_resistor_5_node, pull_resistor_6_node, pull_resistor_7_node, pull_resistor_8_node,
       pull_resistor_9_node, pull_resistor_10_node, pull_resistor_11_node, pull_resistor_12_node,
       pull_resistor_13_node, pull_resistor_14_node, pull_resistor_15_node, pull_resistor_16_node,
       pull_resistor_18_node, pull_resistor_19_node, pull_resistor_20_node, pull_resistor_21_node,
       pull_resistor_22_node, pull_resistor_23_node, READ_B, TRANSPARENCY_B, WRITE_B1, WRITE_B2, WRITE_ENABLE;
  wire [3:0] lvc161_1_p7, lvc161_2_p7, lvc161_3_p7, lvc161_4_p7, lvc161_5_p7, lvc161_6_p7, lvc161_7_p7,
       lvc161_8_p7, lvc163_1_p6;
  wire [7:0] lvc138_1_p5, ram_1_data_2;
  wire [7:4] ram_1_data;
  wire [23:0] DESTINATION_ADDRESS;

  Clock clock_1 (.out(clock_1_out));
  Pull_Resistor pull_resistor_1 (.node(TRANSPARENCY_B));
  Pull_Resistor #(.pull(1)) pull_resistor_2 (.node(CNT));
  Pull_Resistor pull_resistor_3 (.node(FOUR_BIT));
  // DS1813 ds1813_1: pin names not known; wires that end beside it: clock_1_out, ds1813_1_p2, ds1813_1_p2
  Clock clock_2 (.out(clock_2_out));
  not not_1 (not_1_out, clock_2_out);
  D_Flip_Flop d_ff_1 (.clk(clock_2_out), .D(ds1813_1_p2), .Q(d_ff_1_q), .Qn(d_ff_1_qn));  // open: preset, reset
  D_Flip_Flop d_ff_2 (.clk(not_1_out), .D(d_ff_1_qn), .Q(d_ff_2_q));  // open: Qn, preset, reset
  or or_1 (or_1_out, WRITE_B1, WRITE_B2);
  and and_1 (LE, d_ff_1_q, d_ff_2_q);
  Pull_Resistor #(.pull(1)) pull_resistor_4 (.node(pull_resistor_4_node));
  Pull_Resistor #(.pull(1)) pull_resistor_5 (.node(pull_resistor_5_node));
  Pull_Resistor #(.pull(1)) pull_resistor_6 (.node(pull_resistor_6_node));
  Pull_Resistor #(.pull(1)) pull_resistor_7 (.node(pull_resistor_7_node));
  // Probe on DESTINATION_ADDRESS
  RAM #(.addrWidth(24), .databus("bidir"), .enables("line"), .trigger("high"), .\type ("nonvolatile")) ram_1 (
    .addr(DESTINATION_ADDRESS), .data({ram_1_data, ram_1_data_2[3:0]}));  // open: we, oe, clk
  // NOT_Gate not_2 has open pins: in=READ_B, out=open
  // NOT_Gate not_3 has open pins: in=or_1_out, out=open
  // NOT_Gate not_4 has open pins: in=pull_resistor_8_node, out=open
  Pull_Resistor pull_resistor_8 (.node(pull_resistor_8_node));
  not not_5 (PEB, LE);
  // LVC16244 lvc16244_1: pin names not known
  Pull_Resistor #(.pull(1)) pull_resistor_9 (.node(pull_resistor_9_node));
  // LVC161 lvc161_1: pin names not known; wires that end beside it: pull_resistor_4_node, PEB, 4'b0111, CLK, pull_resistor_5_node, CNT, lvc161_1_p7, lvc161_1_p8
  // LVC161 lvc161_2: pin names not known; wires that end beside it: pull_resistor_6_node, PEB, 4'b0000, CLK, pull_resistor_7_node, CNT, lvc161_2_p7, lvc161_2_p8
  // LVC163 lvc163_1: pin names not known; wires that end beside it: ds1813_1_p2, pull_resistor_9_node, clock_2_out, pull_resistor_9_node, CNT, lvc163_1_p6
  Pull_Resistor #(.pull(1)) pull_resistor_10 (.node(pull_resistor_10_node));
  Pull_Resistor #(.pull(1)) pull_resistor_11 (.node(pull_resistor_11_node));
  // LVC161 lvc161_3: pin names not known; wires that end beside it: pull_resistor_10_node, PEB, 4'b1010, CLK, lvc161_1_p8, CNT, lvc161_3_p7, lvc161_3_p8
  // LVC161 lvc161_4: pin names not known; wires that end beside it: pull_resistor_11_node, PEB, 4'b0000, CLK, lvc161_2_p8, CNT, lvc161_4_p7, lvc161_4_p8
  // LVC257 lvc257_1: pin names not known
  Pull_Resistor pull_resistor_12 (.node(pull_resistor_12_node));
  Pull_Resistor #(.pull(1)) pull_resistor_13 (.node(pull_resistor_13_node));
  Pull_Resistor #(.pull(1)) pull_resistor_14 (.node(pull_resistor_14_node));
  Pull_Resistor #(.pull(1)) pull_resistor_15 (.node(pull_resistor_15_node));
  // LVC138 lvc138_1: pin names not known; wires that end beside it: pull_resistor_12_node, pull_resistor_12_node, lvc163_1_p6[2:0], pull_resistor_13_node, {lvc138_1_p5[7:3], WRITE_B1, lvc138_1_p5[1:0]}
  // LVC161 lvc161_5: pin names not known; wires that end beside it: pull_resistor_14_node, PEB, 4'b0011, CLK, lvc161_3_p8, CNT, lvc161_5_p7, lvc161_5_p8
  // LVC161 lvc161_6: pin names not known; wires that end beside it: pull_resistor_15_node, PEB, 4'b0000, CLK, lvc161_4_p8, CNT, lvc161_6_p7, lvc161_6_p8
  Pull_Resistor pull_resistor_16 (.node(pull_resistor_16_node));
  not not_6 (not_6_out, READ_B);
  Pull_Resistor pull_resistor_17 (.node(ram_1_data_2[7:4]));
  // LVC573 lvc573_1: pin names not known; wires that end beside it: pull_resistor_16_node, {ram_1_data, ram_1_data_2[3:0]}, not_6_out, lvc573_1_p4
  // LVC573 lvc573_2: pin names not known; wires that end beside it: ram_1_data_2
  and and_2 (READ_B, lvc138_1_p5[0], lvc138_1_p5[1]);
  not not_7 (WRITE_ENABLE, lvc138_1_p5[1]);
  not not_8 (CLK, lvc138_1_p5[3]);
  Pull_Resistor #(.pull(1)) pull_resistor_18 (.node(pull_resistor_18_node));
  Pull_Resistor #(.pull(1)) pull_resistor_19 (.node(pull_resistor_19_node));
  // Probe on lvc573_1_p4
  Pull_Resistor pull_resistor_20 (.node(pull_resistor_20_node));
  // LVC161 lvc161_7: pin names not known; wires that end beside it: pull_resistor_18_node, PEB, 4'b1111, CLK, lvc161_5_p8, CNT, lvc161_7_p7
  // LVC161 lvc161_8: pin names not known; wires that end beside it: pull_resistor_19_node, PEB, 4'b0110, CLK, lvc161_6_p8, CNT, lvc161_8_p7
  // LVC4245 lvc4245_1: pin names not known; wires that end beside it: WRITE_B1, lvc573_1_p4, pull_resistor_20_node, lvc4245_1_p4, lvc4245_1_p4
  Pull_Resistor pull_resistor_21 (.node(pull_resistor_21_node));
  Pull_Resistor pull_resistor_22 (.node(pull_resistor_22_node));
  Pull_Resistor pull_resistor_23 (.node(pull_resistor_23_node));
  // LVC573 lvc573_3: pin names not known; wires that end beside it: READ_B, 8'h1, LE, DESTINATION_ADDRESS[23:16]
  // LVC164245 lvc164245_1: pin names not known; wires that end beside it: READ_B, READ_B, {lvc161_7_p7, lvc161_5_p7}, pull_resistor_21_node, {lvc161_3_p7, lvc161_1_p7}, pull_resistor_21_node, DESTINATION_ADDRESS[15:8], DESTINATION_ADDRESS[7:0]
  // LVC573 lvc573_4: pin names not known; wires that end beside it: WRITE_B1, {8{1'b0}}, LE, DESTINATION_ADDRESS[23:16]
  // LVC164245 lvc164245_2: pin names not known; wires that end beside it: WRITE_B1, WRITE_B1, {lvc161_8_p7, lvc161_6_p7}, pull_resistor_22_node, {lvc161_4_p7, lvc161_2_p7}, pull_resistor_22_node, DESTINATION_ADDRESS[15:8], DESTINATION_ADDRESS[7:0]
  // F521 f521_1: pin names not known; wires that end beside it: pull_resistor_23_node, lvc573_1_p4, {8{1'b0}}, f521_1_p4
  or or_2 (or_2_out, ~f521_1_p4, TRANSPARENCY_B);  // OR_Gate
  D_Flip_Flop d_ff_3 (.clk(WRITE_ENABLE), .D(or_2_out), .Qn(WRITE_B2));  // open: Q, preset, reset

  // Other names for the same wires on the sheet: SOURCE_ADDRESS[23:0] = DESTINATION_ADDRESS
endmodule
