// Logisim project Simple_65816.circ as structural Verilog: 1 circuit, main circuit main
module main (
);

  wire clock_1_out, IRQ_B, microprocessor_w65c816_1_p7, microprocessor_w65c816_1_p12, NMI_B, not_1_out,
       not_2_out, pull_resistor_1_node, pull_resistor_3_node, pull_resistor_4_node, RDY, RESET, RWB, VDA,
       VP_B, VPA;
  wire [7:0] D, microprocessor_w65c816_1_p6, microprocessor_w65c816_1_p6_2, n8_bit_latch_lvc573_1_p4;

  Clock clock_1 (.out(clock_1_out));
  Pull_Resistor #(.pull(1)) pull_resistor_1 (.node(pull_resistor_1_node));
  // Microprocessor__W65C816 microprocessor_w65c816_1: pin names not known; wires that end beside it: pull_resistor_1_node, IRQ_B, NMI_B, RESET, clock_1_out, {microprocessor_w65c816_1_p6_2, microprocessor_w65c816_1_p6}, microprocessor_w65c816_1_p7, RWB, RDY, VDA, VPA, microprocessor_w65c816_1_p12, VP_B
  // Probe on {microprocessor_w65c816_1_p6_2, microprocessor_w65c816_1_p6}
  // Probe on microprocessor_w65c816_1_p7
  Pull_Resistor #(.pull(1)) pull_resistor_2 (.node(microprocessor_w65c816_1_p12));
  Pull_Resistor pull_resistor_3 (.node(pull_resistor_3_node));
  not not_1 (not_1_out, clock_1_out);
  // _8_bit_Latch__LVC573 8_bit_latch_lvc573_1: pin names not known; wires that end beside it: pull_resistor_3_node, microprocessor_w65c816_1_p7, not_1_out, n8_bit_latch_lvc573_1_p4
  // _8_bit_Bus_Transceiver__LVC4245 8_bit_bus_transceiver_lvc4245_1: pin names not known; wires that end beside it: clock_1_out, microprocessor_w65c816_1_p7, RWB, D
  // Probe on n8_bit_latch_lvc573_1_p4
  not not_2 (not_2_out, RWB);
  // Probe on {n8_bit_latch_lvc573_1_p4[0], microprocessor_w65c816_1_p6_2, microprocessor_w65c816_1_p6}
  RAM #(.addrWidth(17), .databus("bidir"), .enables("line"), .trigger("high"), .\type ("nonvolatile")) ram_1 (
    .addr({n8_bit_latch_lvc573_1_p4[0], microprocessor_w65c816_1_p6_2, microprocessor_w65c816_1_p6}), .data(D));  // open: we, oe, clk
  // NOT_Gate not_3 has open pins: in=not_2_out, out=open
  // NOT_Gate not_4 has open pins: in=RWB, out=open
  Pull_Resistor pull_resistor_4 (.node(pull_resistor_4_node));
  // NOT_Gate not_5 has open pins: in=pull_resistor_4_node, out=open
  // Probe on D
endmodule
