// Logisim project functional_tests.circ as structural Verilog: 2 circuits, main circuit main
module main (
  input  Continue
);

  wire and_2_out, and_3_out, Break_1, Break_2, Break_3, clock_1_out, Clock_Enabled, NMI_out, not_1_out,
       not_2_out, not_3_out, not_4_out, PHI2, pull_resistor_1_node, Reset_out, start_address_1_active,
       Success, w65c02s_expert_1_p5;
  wire [7:0] controlled_buffer_1_out, ram_1_dout, w65c02s_expert_1_p6;
  wire [15:0] Address;
  wire [23:0] Tick_Count;

  Pull_Resistor pull_resistor_1 (.node(pull_resistor_1_node));
  Clock clock_1 (.out(clock_1_out));
  Button Reset (.out(Reset_out));
  Button NMI (.out(NMI_out));
  Counter #(.max('hffffff), .width(24)) counter_1 (.Q(Tick_Count), .clk(PHI2));  // open: load, D, count, carry, up, clr
  and and_1 (PHI2, clock_1_out, Clock_Enabled);
  not not_1 (not_1_out, Reset_out);
  not not_2 (not_2_out, pull_resistor_1_node);
  not not_3 (not_3_out, NMI_out);
  Comparator #(.width(16)) comparator_1 (.a(Address), .b(16'h3469), .eq(Success));  // open: gt, lt
  LED u_Success (.in(Success));
  Comparator #(.width(24)) comparator_2 (.a(Tick_Count), .b(24'h13fdf), .eq(Break_1));  // open: gt, lt
  LED led_1 (.in(Break_1));
  Comparator #(.width(16)) comparator_3 (.a(Address), .b(16'h9f5), .eq(Break_2));  // open: gt, lt
  LED led_2 (.in(Break_2));
  Comparator #(.width(16)) comparator_4 (.a(Address), .b(16'h37b5), .eq(Break_3));  // open: gt, lt
  LED led_3 (.in(Break_3));
  // W65C02S__Expert w65c02s_expert_1: pin names not known; wires that end beside it: not_2_out, not_3_out, not_1_out, PHI2, w65c02s_expert_1_p5, w65c02s_expert_1_p6, Address
  and and_2 (and_2_out, ~Success, ~Break_1, ~Break_2, ~Break_3);  // AND_Gate
  or or_1 (Clock_Enabled, Continue, and_2_out);
  not not_4 (not_4_out, w65c02s_expert_1_p5);
  RAM #(.addrWidth(16), .enables("line")) ram_1 (
    .addr(Address), .we(not_4_out), .clk(PHI2), .din(controlled_buffer_1_out), .dout(ram_1_dout));
  assign controlled_buffer_1_out = not_4_out ? w65c02s_expert_1_p6 : 8'bz;  // Controlled_Buffer controlled_buffer_1
  // Probe on Address
  // Probe on w65c02s_expert_1_p6
  LED Read (.in(w65c02s_expert_1_p5));
  LED Write (.in(w65c02s_expert_1_p5));
  start_address start_address_1 (
    .Data(w65c02s_expert_1_p6), .Active(start_address_1_active), .Clock(PHI2), .Address(16'h400));
  assign w65c02s_expert_1_p6 = and_3_out ? ram_1_dout : 8'bz;  // Controlled_Buffer controlled_buffer_2
  and and_3 (and_3_out, w65c02s_expert_1_p5, start_address_1_active);

  // Notes on the sheet:
  //   Address
  //   Data
  //   Initial Address
endmodule

module start_address (
  input  Clock,
  input  [15:0] Address,
  output [7:0] Data,
  output Active
);

  wire comparator_1_eq, comparator_2_eq, or_1_out;
  wire [23:0] counter_1_q;

  Counter #(.max('hffffff), .width(24)) counter_1 (
    .Q(counter_1_q), .clk(Clock));  // open: load, D, count, carry, up, clr
  assign Data = comparator_1_eq ? Address[7:0] : 8'bz;  // Controlled_Buffer controlled_buffer_1
  Comparator #(.width(24)) comparator_1 (.a(counter_1_q), .b(24'h4), .eq(comparator_1_eq));  // open: gt, lt
  assign Data = comparator_2_eq ? Address[15:8] : 8'bz;  // Controlled_Buffer controlled_buffer_2
  Comparator #(.width(24)) comparator_2 (.a(counter_1_q), .b(24'h5), .eq(comparator_2_eq));  // open: gt, lt
  or or_1 (or_1_out, comparator_1_eq, comparator_2_eq);
  not not_1 (Active, or_1_out);
endmodule
