// Logisim project demo.circ as structural Verilog: 1 circuit, main circuit main
module main (
);

  wire and_1_out, and_2_out, and_3_out, and_4_out, clock_1_out, counter_1_carry, dipswitch_1_p1,
       dipswitch_1_p2, dipswitch_1_p3, dipswitch_1_p4, dipswitch_1_p5, not_1_out, not_2_out, not_4_out,
       not_5_out, not_6_out, or_1_out, pull_resistor_2_node, w65c816s_2_p1, w65c816s_2_p2, w65c816s_2_p3,
       w65c816s_2_p13, w65c816s_2_p14, w65c816s_2_p15, w65c816s_2_p16, w65c816s_2_p17, w65c816s_2_p18;
  wire [7:0] w65c816s_2_p12;
  wire [15:0] w65c816s_2_p11;

  Clock clock_1 (.out(clock_1_out));
  Counter #(.max('h1), .width(1)) counter_1 (
    .carry(counter_1_carry), .clk(and_1_out));  // open: load, D, count, Q, up, clr
  and and_1 (and_1_out, clock_1_out, not_1_out);
  not not_1 (not_1_out, counter_1_carry);
  // DipSwitch #(.number(4)) dipswitch_1: pin names not known; wires that end beside it: dipswitch_1_p1, dipswitch_1_p2, dipswitch_1_p3, dipswitch_1_p4, dipswitch_1_p5
  not not_2 (not_2_out, dipswitch_1_p4);
  and and_2 (and_2_out, counter_1_carry, not_2_out);
  not not_3 (dipswitch_1_p5, dipswitch_1_p1);
  not not_4 (not_4_out, dipswitch_1_p2);
  not not_5 (not_5_out, dipswitch_1_p3);
  // W65C816S w65c816s_1: pin names not known
  // W65C816S w65c816s_2: pin names not known; wires that end beside it: w65c816s_2_p1, w65c816s_2_p2, w65c816s_2_p3, not_4_out, not_5_out, and_2_out, clock_1_out, w65c816s_2_p1, w65c816s_2_p2, w65c816s_2_p3, w65c816s_2_p11, w65c816s_2_p12, w65c816s_2_p13, w65c816s_2_p14, w65c816s_2_p15, w65c816s_2_p16, w65c816s_2_p17, w65c816s_2_p18, w65c816s_2_p14, w65c816s_2_p17
  Register #(.trigger("high")) register_1 (.D(w65c816s_2_p12), .clk(clock_1_out));  // open: en, Q, clr
  Pull_Resistor #(.pull(1)) pull_resistor_1 (.node(w65c816s_2_p18));
  // LVC4245 lvc4245_1: pin names not known
  not not_6 (not_6_out, w65c816s_2_p13);
  or or_1 (or_1_out, w65c816s_2_p15, w65c816s_2_p16);
  and and_3 (and_3_out, clock_1_out, or_1_out, w65c816s_2_p13);
  and and_4 (and_4_out, clock_1_out, not_6_out);
  // Probe on w65c816s_2_p12
  // Probe on w65c816s_2_p11
  RAM #(.addrWidth(16), .databus("bidir"), .enables("line"), .trigger("high"), .\type ("nonvolatile")) ram_1 (
    .addr(w65c816s_2_p11), .data(w65c816s_2_p12));  // open: we, oe, clk
  Pull_Resistor #(.pull(1)) pull_resistor_2 (.node(pull_resistor_2_node));
endmodule
